// Logisim project cpu.circ as structural Verilog: 2 circuits, main circuit main
module main (
  output [7:0] flags,
  output [15:0] PC,
  output [7:0] A,
  output halt,
  output [15:0] insn,
  output [7:0] B
);

  wire and_1_out, clock_1_out, clock_2_out, clock_3_out, clock_4_out, clock_5_out, flags_ov, flags_z,
       not_1_out, or_1_out, or_2_out, ROM_sel, undriven, undriven_2;
  wire [7:0] alu_x, memdata, multiplexer_3_out;
  wire [15:0] adder_1_out, bit_extender_1_out, multiplexer_1_out;

  // Probe on PC
  // Probe on insn[7:0]
  // Probe on insn[15:8]
  and and_1 (and_1_out, insn[7], flags[0]);
  Multiplexer #(.width(16)) multiplexer_1 (
    .in0(16'h1), .in1(bit_extender_1_out), .out(multiplexer_1_out), .sel(or_1_out), .en(1'b1));
  assign bit_extender_1_out = {{8{insn[15]}}, insn[15:8]};  // Bit_Extender bit_extender_1
  or or_1 (or_1_out, insn[0], and_1_out);
  // Probe on insn[15:8]
  // Probe on memdata
  Adder #(.width(16)) adder_1 (.a(PC), .b(multiplexer_1_out), .out(adder_1_out));  // open: cin, cout
  // Probe on A
  // Probe on B
  Register #(.width(16)) u_PC (.D(adder_1_out), .Q(PC), .clk(clock_1_out));  // open: en, clr
  Clock clock_1 (.out(clock_1_out));
  rom ROM (.A(PC), .sel(ROM_sel), .D(insn));
  // Probe on insn
  Comparator #(.width(16), .mode("unsigned")) comparator_1 (.a(insn), .b(16'h1), .eq(halt));  // open: gt, lt
  or or_2 (or_2_out, insn[2], insn[3]);
  Clock clock_2 (.out(clock_2_out));
  Register u_flags (.D({{6{1'b0}}, flags_ov, flags_z}), .en(or_2_out), .Q(flags), .clk(clock_3_out));  // open: clr
  Clock clock_3 (.out(clock_3_out));
  not not_1 (not_1_out, insn[1]);
  LED z (.in(flags[0]));
  LED ov (.in(flags[1]));
  Multiplexer #(.width(8)) multiplexer_2 (.in0(A), .in1(B), .out(memdata), .sel(insn[5]), .en(insn[1]));
  RAM ram_1 (.addr(insn[15:8]), .data(memdata), .sel(1'b1), .clk(clock_2_out), .ld(not_1_out));  // open: clr
  Multiplexer #(.select(2), .width(8)) multiplexer_3 (
    .in0(memdata), .in1(insn[15:8]), .in2(alu_x), .in3(alu_x), .out(multiplexer_3_out),
    .sel({insn[6], insn[4]}));  // open: en
  Comparator comparator_2 (.a({8{1'b0}}), .b(multiplexer_3_out), .eq(flags_z));  // open: gt, lt
  Register register_1 (.D(multiplexer_3_out), .en(insn[2]), .Q(A), .clk(clock_4_out), .clr(undriven));
  Clock clock_4 (.out(clock_4_out));
  Register register_2 (.D(multiplexer_3_out), .en(insn[3]), .Q(B), .clk(clock_5_out), .clr(undriven_2));
  Clock clock_5 (.out(clock_5_out));
  alu alu (.A(A), .B(B), .op(insn[8]), .ov(flags_ov), .X(alu_x));
  // also tied to VCC on the sheet: ROM_sel

  // Other names for the same wires on the sheet: ctl[7:0] = insn[7:0]; ctl_ldmem_ldimm = insn[4]; ctl_ldalu = insn[6];
  //   rflags_z = flags[0]; ctl_jmp = insn[0]; ctl_mwr = insn[1]; ctl_wra = insn[2]; ctl_wrb = insn[3];
  //   ctl_sta_stb = insn[5]; ctl_jz = insn[7]; alu_op = insn[8]; imm[7:0] = insn[15:8]; memaddr[7:0] = insn[15:8]
endmodule

module alu (
  input  [7:0] A,
  input  [7:0] B,
  input  op,
  output ov,
  output [7:0] X
);

  wire [7:0] adder_1_out, subtractor_1_out;

  Subtractor subtractor_1 (.a(A), .b(B), .out(subtractor_1_out), .bin(1'b0), .bout(ov));
  Adder adder_1 (.a(A), .b(B), .out(adder_1_out), .cin(1'b0), .cout(ov));
  Multiplexer #(.width(8)) multiplexer_1 (.in0(adder_1_out), .in1(subtractor_1_out), .out(X), .sel(op));  // open: en
endmodule
