// Logisim project rom.circ as structural Verilog: 1 circuit, main circuit rom
module rom (
  input  [15:0] A,
  output [15:0] D,
  output sel
);

  ROM #(.addrWidth(16), .dataWidth(16)) rom_1 (.addr(A), .data(D), .sel(sel));

  // Notes on the sheet:
  //   contents of rom_1 (hex, n*v repeats v):
  //   0 0 0 1
endmodule
